# Fritzing sketch Layout SAMs 2 (saved by Fritzing 1.0.3b)

parts:
  Mod1 = Amica NodeMCU DEVKIT 1.0
  VCC1 = 4 x AAA Battery Mount [internal_resistance=0.1Ω]
  Part1 = Soil Moisture Sensor
  DHT1 = DHT11 Humitidy and Temperature Sensor
  Q1 = NPN-Transistor [package="TO92 [THT]"]
  M1 = DC Motor [voltage_(max)=6V voltage_(min)=3V]
  R1 = Resistor [tolerance=±5% resistance=330 package="0402 [SMD]"]
  C1 = Capacitor [package=cap-pth-small2]
  D1 = Rectifier Diode [package="Melf DO-213 AA [SMD]"]

nets:
  VCC: Mod1.pin1, Mod1.pin_10, Mod1.pin_26, Part1.VCC, DHT1.VDD
  GND: Mod1.pin2, Mod1.pin_9, Mod1.pin_25, Mod1.pin_29, VCC1.-, Part1.GND, DHT1.GND, Q1.E, Q1.B, Q1.C, R1.Pin_0, D1.cathode
  N1: Mod1.pin8, R1.Pin_1
  N2: Mod1.pin_11, DHT1.DATA
  N3: Mod1.pin_16, Part1.SIG
  N4: Mod1.pin_30, VCC1.+, M1.pin_1, C1.2
  N5: M1.pin_2, C1.1, D1.anode

notes:
  Resistance must be chosen based on power supply voltage
  Collector
  Emitter
  330 Ω
  Noise Filtering Cap.
  Diode

custom parts:
  DHT11 Humitidy and Temperature Sensor: DHT11 Humidity and Temperature Sensor

// code stored in the sketch: Untitled.ino
#include "DHT.h"


#define BLYNK_TEMPLATE_ID "TMPL30PObJad0"
#define BLYNK_TEMPLATE_NAME "SAMs"
#define BLYNK_AUTH_TOKEN "YmB9kZNUSawoHzqcH_iNht18idGLpZbJ"


#include <ESP8266WiFi.h>
#include <BlynkSimpleEsp8266.h>


BlynkTimer timer;
DHT dht(D4, DHT11);
float humd, temp, indx, mois;


void setup() {
  Serial.begin(115200);
  Blynk.begin(BLYNK_AUTH_TOKEN, "AMS", "Monu@123");
  timer.setInterval(2000, send);
  dht.begin();
}


void loop() {
  Blynk.run();
  timer.run();
  humd = dht.readHumidity();
  temp = dht.readTemperature();
  indx = dht.computeHeatIndex(temp, humd);
  mois = (100 - ((analogRead(A0) / 1023.00) * 100));
}


void send() {


  Blynk.virtualWrite(V0, humd);
  Blynk.virtualWrite(V1, temp);
  Blynk.virtualWrite(V2, indx);
  Blynk.virtualWrite(V3, mois);


  Serial.print("Humidity (%): ");
  Serial.println((float)humd, 2);
  Serial.print("Temperature  (C): ");
  Serial.println((float)temp, 2);
  Serial.print("Feels like (Heat Index) (C) : ");
  Serial.println((float)indx, 2);
  Serial.print("Soil Moisture (%) = ");
  Serial.println((float)mois, 2);


  Serial.println("Sent to Cloud");
  Serial.print("\n\n");
}
